// Logisim project Week 2 les 2 Opdracht C.circ as structural Verilog: 1 circuit, main circuit main
module main (
  input  in_1,
  input  in_2,
  input  in_3,
  input  in_4
);

  wire and_1_out, or_1_out, xor_1_out;

  or or_1 (or_1_out, in_3, in_4);
  and and_1 (and_1_out, in_1, in_1, in_2);
  xor xor_1 (xor_1_out, and_1_out, or_1_out);
  LED led_1 (.in(xor_1_out));
endmodule
